// Logisim project game_of_life.circ as structural Verilog: 2 circuits, main circuit main
module game_of_life_cell (
  input  SET,
  input  CLK,
  input  RST,
  input  NW,
  input  N,
  input  NE,
  input  W,
  input  E,
  input  SW,
  input  S,
  input  SE,
  output D
);

  wire and_1_out, comparator_1_eq, comparator_2_eq, or_1_out, or_2_out;
  wire [3:0] bitadder_1_out;

  or or_1 (or_1_out, or_2_out, SET);
  Register #(.width(1)) register_1 (.D(or_1_out), .en(1'b1), .clk(CLK), .Q(D), .clr(RST));
  BitAdder bitadder_1 (.in0({SE, S, SW, E, W, NE, N, NW}), .out(bitadder_1_out));
  Comparator #(.width(4)) comparator_1 (.a(bitadder_1_out), .b(4'b0010), .eq(comparator_1_eq));  // open: gt, lt
  Comparator #(.width(4)) comparator_2 (.a(bitadder_1_out), .b(4'b0011), .eq(comparator_2_eq));  // open: gt, lt
  and and_1 (and_1_out, D, comparator_1_eq);
  or or_2 (or_2_out, and_1_out, comparator_2_eq);
endmodule

module main (
  input  in_1,
  input  in_2,
  input  in_3,
  input  in_4,
  input  RESET,
  input  in_6,
  input  in_7,
  input  in_8,
  input  in_9,
  input  in_10,
  input  in_11,
  input  in_12,
  input  in_13,
  input  in_14,
  input  in_15,
  input  in_16,
  input  in_17
);

  wire C11, C12, C13, C14, C21, C22, C23, C24, C31, C32, C33, C34, C41, C42, C43, C44, CLK;

  Clock clock_1 (.out(CLK));
  game_of_life_cell game_of_life_cell_1 (
    .SET(in_1), .CLK(CLK), .RST(RESET), .NW(C44), .N(C41), .NE(C42), .W(C14), .E(C12), .SW(C24), .S(C21),
    .SE(C22), .D(C11));
  game_of_life_cell game_of_life_cell_2 (
    .SET(in_6), .CLK(CLK), .RST(RESET), .NW(C44), .N(C11), .NE(C12), .W(C24), .E(C22), .SW(C34), .S(C31),
    .SE(C32), .D(C21));
  game_of_life_cell game_of_life_cell_3 (
    .SET(in_10), .CLK(CLK), .RST(RESET), .NW(C24), .N(C21), .NE(C22), .W(C34), .E(C32), .SW(C44), .S(C41),
    .SE(C42), .D(C31));
  game_of_life_cell game_of_life_cell_4 (
    .SET(in_14), .CLK(CLK), .RST(RESET), .NW(C34), .N(C31), .NE(C32), .W(C44), .E(C42), .SW(C14), .S(C11),
    .SE(C12), .D(C41));
  LED led_1 (.in(C11));
  LED led_2 (.in(C21));
  LED led_3 (.in(C31));
  LED led_4 (.in(C41));
  LED led_5 (.in(C12));
  LED led_6 (.in(C22));
  LED led_7 (.in(C32));
  LED led_8 (.in(C42));
  game_of_life_cell game_of_life_cell_5 (
    .SET(in_2), .CLK(CLK), .RST(RESET), .NW(C41), .N(C42), .NE(C43), .W(C11), .E(C13), .SW(C21), .S(C22),
    .SE(C23), .D(C12));
  game_of_life_cell game_of_life_cell_6 (
    .SET(in_7), .CLK(CLK), .RST(RESET), .NW(C11), .N(C12), .NE(C13), .W(C21), .E(C23), .SW(C31), .S(C32),
    .SE(C33), .D(C22));
  game_of_life_cell game_of_life_cell_7 (
    .SET(in_11), .CLK(CLK), .RST(RESET), .NW(C21), .N(C22), .NE(C23), .W(C21), .E(C23), .SW(C41), .S(C42),
    .SE(C43), .D(C32));
  game_of_life_cell game_of_life_cell_8 (
    .SET(in_15), .CLK(CLK), .RST(RESET), .NW(C31), .N(C32), .NE(C33), .W(C41), .E(C43), .SW(C11), .S(C12),
    .SE(C13), .D(C42));
  LED led_9 (.in(C13));
  LED led_10 (.in(C23));
  LED led_11 (.in(C33));
  LED led_12 (.in(C43));
  LED led_13 (.in(C14));
  LED led_14 (.in(C24));
  LED led_15 (.in(C34));
  LED led_16 (.in(C44));
  game_of_life_cell game_of_life_cell_9 (
    .SET(in_3), .CLK(CLK), .RST(RESET), .NW(C42), .N(C43), .NE(C44), .W(C12), .E(C14), .SW(C22), .S(C23),
    .SE(C24), .D(C13));
  game_of_life_cell game_of_life_cell_10 (
    .SET(in_8), .CLK(CLK), .RST(RESET), .NW(C12), .N(C13), .NE(C14), .W(C22), .E(C24), .SW(C32), .S(C33),
    .SE(C34), .D(C23));
  game_of_life_cell game_of_life_cell_11 (
    .SET(in_12), .CLK(CLK), .RST(RESET), .NW(C22), .N(C23), .NE(C24), .W(C32), .E(C34), .SW(C42), .S(C43),
    .SE(C44), .D(C33));
  game_of_life_cell game_of_life_cell_12 (
    .SET(in_16), .CLK(CLK), .RST(RESET), .NW(C32), .N(C33), .NE(C34), .W(C42), .E(C43), .SW(C12), .S(C13),
    .SE(C14), .D(C43));
  game_of_life_cell game_of_life_cell_13 (
    .SET(in_4), .CLK(CLK), .RST(RESET), .NW(C43), .N(C44), .NE(C41), .W(C13), .E(C11), .SW(C23), .S(C24),
    .SE(C21), .D(C14));
  game_of_life_cell game_of_life_cell_14 (
    .SET(in_9), .CLK(CLK), .RST(RESET), .NW(C13), .N(C14), .NE(C11), .W(C23), .E(C21), .SW(C33), .S(C34),
    .SE(C31), .D(C24));
  game_of_life_cell game_of_life_cell_15 (
    .SET(in_13), .CLK(CLK), .RST(RESET), .NW(C23), .N(C24), .NE(C21), .W(C33), .E(C31), .SW(C43), .S(C44),
    .SE(C11), .D(C34));
  game_of_life_cell game_of_life_cell_16 (
    .SET(in_17), .CLK(CLK), .RST(RESET), .NW(C33), .N(C34), .NE(C31), .W(C43), .E(C41), .SW(C13), .S(C14),
    .SE(C11), .D(C44));

  // Other names for the same wires on the sheet: RST = RESET
endmodule
